# Fritzing sketch ArduECO (saved by Fritzing 0.9.3b)

parts:
  U1 = NodeMCU V3.0
  Micro_SD_Card_Reader = MicroSD Card Module
  NEO6MV2_GPS_Module = SUP500F [package=sup500f]
  MQ7_SENSOR = MQ GAS SENSOR
  LED1 = LED - 5mm [color="Red (633nm)" package="5 mm [THT]"]
  R1 = Resistor [tolerance=±5% resistance=220 package=THT]
  SEND_BUTTON = Round Pushbutton
  R2 = Resistor [tolerance=±5% resistance=220 package=THT]
  LEDs = LED - 5mm [color="Blue (525nm)" package="5 mm [THT]"]

nets:
  N1: U1.D0, R1.Pin_1
  N2: U1.D1, NEO6MV2_GPS_Module.RX-I
  N3: U1.D2, NEO6MV2_GPS_Module.TX-O
  N4: U1.D3, Micro_SD_Card_Reader.CS
  N5: U1.D4, R2.Pin_1
  VCC: U1.3V3, NEO6MV2_GPS_Module.VCC, MQ7_SENSOR.VCC
  GND: U1.GND#6, U1.GND#13, U1.GND#16, U1.GND#33, NEO6MV2_GPS_Module.GND, MQ7_SENSOR.GND, LED1.cathode, SEND_BUTTON.leg0, LEDs.cathode
  N6: U1.D5, Micro_SD_Card_Reader.SCK
  N7: U1.D6, Micro_SD_Card_Reader.MISO
  N8: U1.D7, Micro_SD_Card_Reader.MOSI
  N9: U1.D8, SEND_BUTTON.leg1
  N10: U1.VU, Micro_SD_Card_Reader.VCC
  N11: U1.GND#41, Micro_SD_Card_Reader.GND
  N12: U1.A0, MQ7_SENSOR.AO
  N13: LED1.anode, R1.Pin_0
  N14: R2.Pin_0, LEDs.anode

custom parts:
  NodeMCU V3.0: ESP8266 based NodeMCU
